# Fritzing sketch brewery_wiring_schematic (saved by Fritzing 0.9.3b)

parts:
  Part1 = Arduino Nano (Rev3.0)
  WeMos_D1_Mini1 = WeMos D1 Mini
  Grove1 = Grove OLED 128x96
  S1 = Round Pushbutton
  LED1 = smd LED [color="Red (635nm)" package="0805 [SMD]"]
  S3 = Toggle Switch [package=THT]
  S4 = Toggle Switch [package=THT]
  HLK-PM1 = HLK-PM01
  RHT1 = Humidity and Temperature Sensor RHT03  # not connected
  F1 = FUSE [package=fuse_5mm]
  DS1 = DS18B20 1-Wire Temperature Sensor [part_number=DS18B20]
  R1 = Resistor [tolerance=±5% resistance=4.7k package="0805 [SMD]"]
  R2 = Resistor [tolerance=±5% resistance=10k package="0805 [SMD]"]
  R3 = Resistor [tolerance=±5% resistance=1M package=THT]
  R4 = Resistor [tolerance=±5% resistance=1M package=THT]
  Power_plug1 = Power plug
  Power_plug2 = Power plug
  U1 = RELAY [package=relay-jzc]
  J1 = Screw terminal - 2 pins [package=THT]
  J2 = Screw terminal - 2 pins [package=THT]
  S7 = Toggle Switch [package=THT]
  U2 = RELAY [package=relay-jzc]
  J4 = Screw terminal - 2 pins [package=THT]  # not connected
  J5 = Screw terminal - 2 pins [package=THT]
  JP1 = Header 3 [package=screwterminal-3.5mm-3_lock.007s]
  JP2 = Header 3 [package=screwterminal-3.5mm-3_lock.007s]
  LED2 = 7-SEGMENT-4DIGIT [package=7-segment-4digit]
  LED3 = 7-SEGMENT-4DIGIT [package=7-segment-4digit]

nets:
  N1: Part1.D6, R1.Pin_1
  N2: Part1.D8, DS1.DQ, R2.Pin_1
  N3: Part1.A1, WeMos_D1_Mini1.D0
  3V3: WeMos_D1_Mini1.3V3, Grove1.VCC
  N4: WeMos_D1_Mini1.D1, Grove1.SCL
  N5: WeMos_D1_Mini1.D2, Grove1.SDA
  N6: WeMos_D1_Mini1.D3, U2.NC
  N7: WeMos_D1_Mini1.D4, U1.NC
  N8: WeMos_D1_Mini1.D5, LED1.anode
  N9: WeMos_D1_Mini1.D6, S1.leg1
  N10: WeMos_D1_Mini1.D7, S3.COM
  N11: WeMos_D1_Mini1.G, Grove1.GND
  N12: S4.L1, Power_plug2.VCC, J1.pin1
  N13: S4.COM, HLK-PM1.AC#0, U1.MAIN
  N14: HLK-PM1.AC#1, F1.2
  N15: HLK-PM1.-Vo, U1.NO, U2.NO
  N16: HLK-PM1.+Vo, U1.COIL2, U2.COIL2
  N17: F1.1, R3.Pin_1, Power_plug2.GND, J1.pin2
  N18: DS1.GND, R1.Pin_0, R2.Pin_0, J5.pin2
  N19: DS1.VDD, JP1.2
  N20: R3.Pin_0, U1.COIL1
  N21: R4.Pin_0, U2.COIL1
  N22: R4.Pin_1, Power_plug1.GND, J2.pin2
  N23: Power_plug1.VCC, J2.pin1, S7.COM
  N24: S7.L1, U2.MAIN
  N25: J5.pin1, JP2.1, LED2.9, LED3.9
